// Logisim project chap6.circ as structural Verilog: 6 circuits, main circuit Von Neumann machine
module Von_Neumann_machine (
  input  reset
);

  wire clock_out, cpu_1_m_we;
  wire [7:0] cpu_1_ma, cpu_1_mdo, ram_1_data;

  CPU cpu_1 (.MA(cpu_1_ma), .MDI(ram_1_data), .MDO(cpu_1_mdo), .M_we(cpu_1_m_we), .ck(clock_out), .reset(reset));
  Clock clock (.out(clock_out));
  // Probe on cpu_1_ma
  // Probe on cpu_1_mdo
  // Probe on ram_1_data
  RAM #(.bus("separate")) ram_1 (
    .addr(cpu_1_ma), .din(cpu_1_mdo), .data(ram_1_data), .str(cpu_1_m_we), .sel(1'b1), .clk(clock_out),
    .ld(1'b1));  // open: clr

  // Notes on the sheet:
  //   processor
  //   system bus
  //   address
  //   data: CPU to memory
  //   data: memory to CPU
  //   control: 1 means "write"
  //   memory
endmodule

module CPU (
  input  [7:0] MDI,
  input  ck,
  input  reset,
  output [7:0] MA,
  output [7:0] MDO,
  output M_we
);

  wire fsm_1_dofetch, fsm_1_doja, fsm_1_dojr, fsm_1_memwrite, fsm_1_wecst, fsm_1_wedestreg, fsm_1_weflags,
       fsm_1_weir, fsm_1_wepc;
  wire [2:0] data_path_1_flags;
  wire [7:0] data_path_1_ir;

  FSM fsm_1 (
    .Instruction(data_path_1_ir), .flags(data_path_1_flags), .weIR(fsm_1_weir), .doFetch(fsm_1_dofetch),
    .memwrite(fsm_1_memwrite), .weDestReg(fsm_1_wedestreg), .wePC(fsm_1_wepc), .weCST(fsm_1_wecst),
    .doJA(fsm_1_doja), .doJR(fsm_1_dojr), .weFlags(fsm_1_weflags), .reset(ck), .clk(reset));
  Data_Path data_path_1 (
    .weIR(fsm_1_weir), .doFetch(fsm_1_dofetch), .memwrite(fsm_1_memwrite), .weDestReg(fsm_1_wedestreg),
    .wePC(fsm_1_wepc), .weCST(fsm_1_wecst), .doJA(fsm_1_doja), .doJR(fsm_1_dojr), .weFlags(fsm_1_weflags),
    .IR(data_path_1_ir), .MA(MA), .MDI(MDI), .MDO(MDO), .M_we(M_we), .Flags(data_path_1_flags), .ck(ck),
    .reset(reset));

  // Notes on the sheet:
  //   FSM (Automate)
  //   Data Path
  //   Instruction
  //   Flags
  //   (memory address)
  //   (data in from mem)
  //   (data out to mem)
  //   (memory write enable)
endmodule

module Data_Path (
  input  weIR,
  input  doFetch,
  input  memwrite,
  input  weDestReg,
  input  wePC,
  input  weCST,
  input  doJA,
  input  doJR,
  input  weFlags,
  input  [7:0] MDI,
  input  ck,
  input  reset,
  output [7:0] IR,
  output [7:0] MA,
  output [7:0] MDO,
  output M_we,
  output [2:0] Flags
);

  wire comparator_1_eq, weA, weB;
  wire [2:0] alu_1_flags;
  wire [7:0] adder_1_out, alu_1_out, multiplexer_2_out, multiplexer_3_out, multiplexer_4_out,
       multiplexer_5_out, regA, regB, regCST, regPC;

  // Probe on MDO
  Multiplexer #(.width(8), .enable("false")) multiplexer_1 (.in0(regA), .in1(regB), .out(MDO), .sel(IR[1]));
  // Probe on multiplexer_2_out
  Multiplexer #(.width(8), .enable("false")) multiplexer_2 (
    .in0(regA), .in1(regCST), .out(multiplexer_2_out), .sel(IR[2]));
  ALU alu_1 (
    .arg1(MDO), .arg2(multiplexer_2_out), .out(alu_1_out), .flags(alu_1_flags), .codeop(IR[6:3]),
    .arg2s(IR[2]));
  Multiplexer #(.width(8), .enable("false")) multiplexer_3 (
    .in0(8'h1), .in1({{4{IR[4]}}, IR[3:0]}), .out(multiplexer_3_out), .sel(doJR));
  Adder adder_1 (.a(regPC), .b(multiplexer_3_out), .out(adder_1_out));  // open: cin, cout
  // Probe on Flags
  Register #(.width(3)) u_flags (.D(alu_1_flags), .en(weFlags), .Q(Flags), .clk(ck), .clr(reset));
  // Probe on alu_1_out
  Multiplexer #(.width(8), .enable("false")) multiplexer_4 (
    .in0(alu_1_out), .in1(MDI), .out(multiplexer_4_out), .sel(comparator_1_eq));
  Comparator #(.width(4)) comparator_1 (.a(IR[6:3]), .b(4'b1101), .eq(comparator_1_eq));  // open: gt, lt
  Multiplexer #(.width(8), .enable("false")) multiplexer_5 (
    .in0(adder_1_out), .in1(regCST), .out(multiplexer_5_out), .sel(doJA));
  Register u_IR (.D(MDI), .en(weIR), .Q(IR), .clk(ck), .clr(reset));
  Register CST (.D(MDI), .en(weCST), .Q(regCST), .clk(ck), .clr(reset));
  // Probe on multiplexer_5_out
  Register PC (.D(multiplexer_5_out), .en(wePC), .Q(regPC), .clk(ck), .clr(reset));
  Register A (.D(multiplexer_4_out), .en(weA), .Q(regA), .clk(ck), .clr(reset));
  Register B (.D(multiplexer_4_out), .en(weB), .Q(regB), .clk(ck), .clr(reset));
  and and_1 (weA, ~IR[0], weDestReg);  // AND_Gate
  and and_2 (weB, IR[0], weDestReg);
  // Probe on multiplexer_2_out
  // Probe on MDI
  Multiplexer #(.width(8), .enable("false")) multiplexer_6 (
    .in0(multiplexer_2_out), .in1(regPC), .out(MA), .sel(doFetch));

  assign M_we = memwrite;

  // Other names for the same wires on the sheet: destS = IR[0]; offset[4:0] = IR[4:0]; arg1S = IR[1]; arg2S = IR[2];
  //   opcode[3:0] = IR[6:3]

  // Notes on the sheet:
  //   (Instruction)
  //   (memory address)
  //   (data out to mem)
  //   (memory write enable)
  //   (data in from mem)
endmodule

module ALU (
  input  [7:0] arg1,
  input  [7:0] arg2,
  input  arg2s,
  input  [3:0] codeop,
  output [2:0] flags,
  output [7:0] out
);


  // Other names for the same wires on the sheet: co3 = codeop[0]; co2 = codeop[1]; co1 = codeop[2]; co0 = codeop[3]
endmodule

module FSM (
  input  [7:0] Instruction,
  input  [2:0] flags,
  input  clk,
  input  reset,
  output weIR,
  output doFetch,
  output memwrite,
  output weDestReg,
  output wePC,
  output weCST,
  output doJA,
  output doJR,
  output weFlags
);
endmodule

module Brouiilon (
);

  wire carryAdd, carrySub;
  wire [7:0] adder_1_out, and_1_out, or_1_out, subtractor_1_out, undriven, undriven_2, undriven_3,
       undriven_4, undriven_5, undriven_6, undriven_7, undriven_8, undriven_9, undriven_10, undriven_11,
       xor_1_out, xor_2_out;
  wire [7:7] undriven_12;

  Adder adder_1 (.a(undriven), .b(undriven_7), .out(adder_1_out), .cin(1'b0), .cout(carryAdd));
  Subtractor subtractor_1 (.a(undriven_2), .b(undriven_8), .out(subtractor_1_out), .bin(1'b0), .bout(carrySub));
  assign and_1_out = undriven_3 & undriven_9;  // AND_Gate and_1, 8 bits wide
  assign or_1_out = undriven_4 | undriven_10;  // OR_Gate or_1, 8 bits wide
  assign xor_1_out = undriven_5 ^ undriven_11;  // XOR_Gate xor_1, 8 bits wide
  assign xor_2_out = undriven_6 ^ {8{undriven_12[7]}};  // XOR_Gate xor_2, 8 bits wide

  // Notes on the sheet:
  //   0000 add
  //   0001 sub
  //   0110 cmp
  //   0010 and
  //   0011 or
  //   0100 xor
  //   0101 lsr
  //   1000 passthrough/invert arg1
endmodule
