// Logisim project chap3.circ as structural Verilog
module Additionneur_1bit (
  input  a,
  input  b,
  input  c_in,
  output S,
  output c_out
);

  wire and_1_out, and_2_out, and_3_out, and_4_out, and_5_out, and_6_out, and_7_out;

  and and_1 (and_1_out, ~a, ~b, c_in);  // AND_Gate
  and and_2 (and_2_out, ~a, b, ~c_in);  // AND_Gate
  and and_3 (and_3_out, a, ~b, ~c_in);  // AND_Gate
  and and_4 (and_4_out, a, b, c_in);
  and and_5 (and_5_out, a, b);
  and and_6 (and_6_out, a, c_in);
  and and_7 (and_7_out, b, c_in);
  or or_1 (S, and_1_out, and_2_out, and_3_out, and_4_out);
  or or_2 (c_out, and_5_out, and_6_out, and_7_out);
endmodule

module Additionneur_8bits (
  input  c_in,
  input  [7:0] A,
  input  [7:0] B,
  output [7:0] S,
  output c_out
);

  wire Add1bit_2_c_out, Add1bit_3_c_out, Add1bit_4_c_out, Add1bit_5_c_out, Add1bit_6_c_out, Add1bit_7_c_out,
       Add1bit_c_out;

  Additionneur_1bit Add1bit (.a(A[0]), .b(B[0]), .c_in(c_in), .c_out(Add1bit_c_out), .S(S[0]));
  Additionneur_1bit Add1bit_2 (.a(A[1]), .b(B[1]), .c_in(Add1bit_c_out), .c_out(Add1bit_2_c_out), .S(S[1]));
  Additionneur_1bit Add1bit_3 (.a(A[2]), .b(B[2]), .c_in(Add1bit_2_c_out), .c_out(Add1bit_3_c_out), .S(S[2]));
  Additionneur_1bit Add1bit_4 (.a(A[3]), .b(B[3]), .c_in(Add1bit_3_c_out), .c_out(Add1bit_4_c_out), .S(S[3]));
  Additionneur_1bit Add1bit_5 (.a(A[4]), .b(B[4]), .c_in(Add1bit_4_c_out), .c_out(Add1bit_5_c_out), .S(S[4]));
  Additionneur_1bit Add1bit_6 (.a(A[5]), .b(B[5]), .c_in(Add1bit_5_c_out), .c_out(Add1bit_6_c_out), .S(S[5]));
  Additionneur_1bit Add1bit_7 (.a(A[6]), .b(B[6]), .c_in(Add1bit_6_c_out), .c_out(Add1bit_7_c_out), .S(S[6]));
  Additionneur_1bit Add1bit_8 (.a(A[7]), .b(B[7]), .c_in(Add1bit_7_c_out), .c_out(c_out), .S(S[7]));
endmodule

module inverseur_1_bit (
  input  c_in,
  input  B,
  output B_prime
);

  wire and_1_out, and_2_out;

  and and_1 (and_1_out, c_in, ~B);  // AND_Gate
  and and_2 (and_2_out, B, ~c_in);  // AND_Gate
  or or_1 (B_prime, and_1_out, and_2_out);

  // Notes on the sheet:
  //   Inverseur 1 bit
endmodule

module Inverseur_8_bits (
  input  c_in,
  input  [7:0] B,
  output [7:0] B_prime
);

  inverseur_1_bit inverseur_1_bit_1 (.B(B[0]), .B_prime(B_prime[0]), .c_in(c_in));
  inverseur_1_bit inverseur_1_bit_2 (.B(B[1]), .B_prime(B_prime[1]), .c_in(c_in));
  inverseur_1_bit inverseur_1_bit_3 (.B(B[2]), .B_prime(B_prime[2]), .c_in(c_in));
  inverseur_1_bit inverseur_1_bit_4 (.B(B[3]), .B_prime(B_prime[3]), .c_in(c_in));
  inverseur_1_bit inverseur_1_bit_5 (.B(B[4]), .B_prime(B_prime[4]), .c_in(c_in));
  inverseur_1_bit inverseur_1_bit_6 (.B(B[5]), .B_prime(B_prime[5]), .c_in(c_in));
  inverseur_1_bit inverseur_1_bit_7 (.B(B[6]), .B_prime(B_prime[6]), .c_in(c_in));
  inverseur_1_bit inverseur_1_bit_8 (.B(B[7]), .B_prime(B_prime[7]), .c_in(c_in));

  // Notes on the sheet:
  //   Inverseur 8 bits
endmodule

module Add_sous_8_bits (
);

  wire additionneur_8bits_1_c_out, undriven_3;
  wire [7:0] additionneur_8bits_1_s, inverseur_8_bits_1_b_prime, undriven, undriven_2;

  Inverseur_8_bits inverseur_8_bits_1 (.B(undriven_2), .B_prime(inverseur_8_bits_1_b_prime), .c_in(undriven_3));
  Additionneur_8bits additionneur_8bits_1 (
    .A(undriven), .B(inverseur_8_bits_1_b_prime), .S(additionneur_8bits_1_s), .c_in(undriven_3),
    .c_out(additionneur_8bits_1_c_out));

  // Notes on the sheet:
  //   A
  //   B
  //   c_in
  //   c_out
  //   S
endmodule
