// Logisim project chap4.circ as structural Verilog
module main (
);

  wire CLK, enable, reset;
  wire [7:0] registre1bit_1_out, undriven;

  registre1bit registre1bit_1 (
    .IN(undriven[0]), .OUT(registre1bit_1_out[0]), .enable(enable), .reset(reset), .CLK(CLK));
  registre1bit registre1bit_2 (
    .IN(undriven[1]), .OUT(registre1bit_1_out[1]), .enable(enable), .reset(reset), .CLK(CLK));
  registre1bit registre1bit_3 (
    .IN(undriven[2]), .OUT(registre1bit_1_out[2]), .enable(enable), .reset(reset), .CLK(CLK));
  registre1bit registre1bit_4 (
    .IN(undriven[3]), .OUT(registre1bit_1_out[3]), .enable(enable), .reset(reset), .CLK(CLK));
  registre1bit registre1bit_5 (
    .IN(undriven[4]), .OUT(registre1bit_1_out[4]), .enable(enable), .reset(reset), .CLK(CLK));
  registre1bit registre1bit_6 (
    .IN(undriven[5]), .OUT(registre1bit_1_out[5]), .enable(enable), .reset(reset), .CLK(CLK));
  registre1bit registre1bit_7 (
    .IN(undriven[6]), .OUT(registre1bit_1_out[6]), .enable(enable), .reset(reset), .CLK(CLK));
  registre1bit registre1bit_8 (
    .IN(undriven[7]), .OUT(registre1bit_1_out[7]), .enable(enable), .reset(reset), .CLK(CLK));

  // Notes on the sheet:
  //   IN
  //   OUT
endmodule

module registre1bit (
  input  IN,
  input  enable,
  input  reset,
  input  CLK,
  output OUT
);

  wire multiplexer_1_out, multiplexer_2_out, multiplexer_3_out;

  Multiplexer #(.enable("false")) multiplexer_1 (.in0(OUT), .in1(IN), .out(multiplexer_1_out), .sel(enable));
  Multiplexer #(.enable("false")) multiplexer_2 (
    .in0(multiplexer_1_out), .in1(1'b0), .out(multiplexer_2_out), .sel(reset));
  Multiplexer #(.enable("false")) multiplexer_3 (
    .in0(multiplexer_2_out), .in1(multiplexer_3_out), .out(multiplexer_3_out), .sel(CLK));
  Multiplexer #(.enable("false")) multiplexer_4 (.in0(OUT), .in1(multiplexer_3_out), .out(OUT), .sel(CLK));
endmodule

module registre8bits (
  input  enable,
  input  reset,
  input  CLK,
  input  [7:0] IN,
  output [7:0] OUT
);

  registre1bit registre1bit_1 (.IN(IN[0]), .OUT(OUT[0]), .enable(enable), .reset(reset), .CLK(CLK));
  registre1bit registre1bit_2 (.IN(IN[1]), .OUT(OUT[1]), .enable(enable), .reset(reset), .CLK(CLK));
  registre1bit registre1bit_3 (.IN(IN[2]), .OUT(OUT[2]), .enable(enable), .reset(reset), .CLK(CLK));
  registre1bit registre1bit_4 (.IN(IN[3]), .OUT(OUT[3]), .enable(enable), .reset(reset), .CLK(CLK));
  registre1bit registre1bit_5 (.IN(IN[4]), .OUT(OUT[4]), .enable(enable), .reset(reset), .CLK(CLK));
  registre1bit registre1bit_6 (.IN(IN[5]), .OUT(OUT[5]), .enable(enable), .reset(reset), .CLK(CLK));
  registre1bit registre1bit_7 (.IN(IN[6]), .OUT(OUT[6]), .enable(enable), .reset(reset), .CLK(CLK));
  registre1bit registre1bit_8 (.IN(IN[7]), .OUT(OUT[7]), .enable(enable), .reset(reset), .CLK(CLK));
endmodule

module Petit_compteur (
);

  registre8bits registre8bits_1 ();  // open: IN, enable, reset, CLK, OUT
endmodule
