// Logisim project Multiplexeur.circ as structural Verilog: 2 circuits, main circuit Multiplexeur 2 vers 1
module Multiplexeur_2_vers_1 (
);

  wire and_1_out, and_2_out, multiplexer_1_out, or_1_out, undriven, undriven_2, undriven_3, undriven_4,
       undriven_5, undriven_6;

  and and_1 (and_1_out, undriven, ~undriven_3);  // AND_Gate
  and and_2 (and_2_out, undriven_3, undriven_2);
  or or_1 (or_1_out, and_1_out, and_2_out);
  Multiplexer #(.disabled(0), .enable("false")) multiplexer_1 (
    .in0(undriven_4), .in1(undriven_5), .out(multiplexer_1_out), .sel(undriven_6));

  // Notes on the sheet:
  //   E0
  //   c
  //   E1
  //   <=>
  //   S
  //   E0
  //   E1
  //   S
  //   c
endmodule

module Multiplexeur_1_vers_2 (
);

  wire and_1_out, and_2_out, demultiplexer_1_out0, demultiplexer_1_out1, undriven, undriven_2, undriven_3,
       undriven_4;

  and and_1 (and_1_out, undriven, ~undriven_2);  // AND_Gate
  and and_2 (and_2_out, undriven_2, undriven);
  Demultiplexer #(.disabled(0), .enable("false")) demultiplexer_1 (
    .out0(demultiplexer_1_out0), .out1(demultiplexer_1_out1), .in(undriven_3), .sel(undriven_4));

  // Notes on the sheet:
  //   c
  //   E
  //   S0
  //   S1
  //   <=>
  //   E
  //   c
  //   S0
  //   S1
endmodule
