// Logisim project porteLogique.circ as structural Verilog: 1 circuit, main circuit main
module main (
);

  wire ET_out, NON_out, OU_out, undriven, undriven_2;

  not NON (NON_out, undriven);
  and ET (ET_out, undriven, undriven_2);
  or OU (OU_out, undriven, undriven_2);

  // Notes on the sheet:
  //   a
  //   b
  //   non(a)
  //   ab
  //   a+b
endmodule
